# Fritzing sketch Shema spajanja (saved by Fritzing 0.9.3b)

parts:
  Mod1 = Raspberry Pi Pico
  Keypad4x1 = Keypad Membran 4x4
  LCD1 = TFT 1.8 inch 160x128 w SD
  Load_Cell1 = Load Cell - Red/white/black/green
  U1 = AD7745 [package=tssop16]

nets:
  N1: Mod1.pin_1, Keypad4x1.Pin4
  N2: Mod1.pin_2, Keypad4x1.Pin3
  N3: Mod1.pin_3, Mod1.pin_23, Mod1.pin_33, Mod1.pin_42, LCD1.pin2, U1.GND
  N4: Mod1.pin_4, Keypad4x1.Pin2
  N5: Mod1.pin_5, Keypad4x1.Pin1
  N6: Mod1.pin_11, U1.NC
  N7: Mod1.pin_12, U1.SDA
  N8: Mod1.pin_20, LCD1.pin_5
  N9: Mod1.pin_22, LCD1.pin3
  N10: Mod1.pin_24, LCD1.pin_7
  N11: Mod1.pin_25, LCD1.pin_6
  N12: Mod1.pin_26, LCD1.pin4
  N13: Mod1.pin_27, Keypad4x1.Pin8
  N14: Mod1.pin_29, Keypad4x1.Pin7
  N15: Mod1.pin_31, Keypad4x1.Pin6
  N16: Mod1.pin_32, Keypad4x1.Pin5
  N17: Mod1.pin_36, U1.VDD
  N18: Mod1.pin_37, LCD1.pin_1
  N19: Load_Cell1.wire1, U1.CIN1+
  N20: Load_Cell1.wire2, U1.CIN1-
  N21: Load_Cell1.wire3, U1.REFIN-
  N22: Load_Cell1.wire4, U1.REFIN+

custom parts:
  Raspberry Pi Pico: Raspberry Pi Pico. Based around the RP2040 microcontroller the Pico is a low cost microcontroller device bringing Raspberry Pi quality, cost, and easy of use to the microcontroller space. Jan 2021, Split part in to two versions: tht (this one) and SMD. This one will drill holes for a .1 in header in pcb to allow plugging in the module as well as providing pads to solder the module to the top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
  Keypad Membran 4x4: Membrane Keypad 4x4 Matrix
  TFT 1.8 inch 160x128 w SD: This is a generic 1.8 tft spi lcd display available on ebay and others. The 1.8" display has 128x160 color pixels.
  Load Cell - Red/white/black/green: A rectangle load cell/weighting pressure Sensor with four wires - Red, white, black, green. Normally corresponding with E+, E-, A+, A- respectively.
